// Digital circuit add4b.dig as structural Verilog
module add4b (
  input  A3,
  input  A2,
  input  A1,
  input  A0,
  input  B3,
  input  B2,
  input  B1,
  input  B0,
  input  Ci,
  output Co,
  output S3,
  output S2,
  output S1,
  output S0
);

  wire fulladder_2_co, fulladder_3_co, fulladder_4_co;

  fulladder fulladder_1 (.A(A3), .B(B3), .Ci(fulladder_2_co), .Co(Co), .S(S3));
  fulladder fulladder_2 (.A(A2), .B(B2), .Ci(fulladder_3_co), .Co(fulladder_2_co), .S(S2));
  fulladder fulladder_3 (.A(A1), .B(B1), .Ci(fulladder_4_co), .Co(fulladder_3_co), .S(S1));
  fulladder fulladder_4 (.A(A0), .B(B0), .Ci(Ci), .Co(fulladder_4_co), .S(S0));
endmodule
