// Digital circuit addsub8b.dig as structural Verilog
module addsub8b (
  input  [7:0] A,
  input  [7:0] B,
  input  sub,
  output [7:0] R,
  output Co
);

  wire [7:0] xor_1_out;

  assign xor_1_out = B ^ {8{sub}};  // XOr xor_1, 8 bits wide
  add8b add8b_1 (.A(A), .B(xor_1_out), .Ci(sub), .S(R), .Co(Co));
endmodule
