// Digital circuit flags.dig as structural Verilog
module flags (
  input  [7:0] A,
  input  [7:0] B,
  input  [7:0] R,
  input  sub,
  output Z,
  output N,
  output O
);

  nor nor_1 (Z, R[0], R[1], R[2], R[3], R[4], R[5], R[6], R[7], 1'b0);
  ovf ovf_1 (.sub(sub), .A7(A[7]), .B7(B[7]), .R7(R[7]), .ovf(O));

  assign N = R[7];
endmodule
