// Digital circuit lab2.dig as structural Verilog
module lab2 (
  input  sub
);

  wire addsub8b_1_co, flags_1_n, flags_1_o, flags_1_z;
  wire [3:0] addsub8b_1_r, addsub8b_1_r_2, dipswitch_1_out, dipswitch_2_out, dipswitch_12_out,
       dipswitch_16_out;

  Seven_Seg_Hex seven_seg_hex_1 (.d(dipswitch_1_out), .dp(1'b0));
  // Probe A on {dipswitch_1_out, dipswitch_2_out}
  DipSwitch dipswitch_1 (.out(dipswitch_1_out[3]));
  Seven_Seg_Hex seven_seg_hex_2 (.d(dipswitch_2_out), .dp(1'b0));
  DipSwitch dipswitch_2 (.out(dipswitch_2_out[3]));
  DipSwitch dipswitch_3 (.out(dipswitch_1_out[0]));
  DipSwitch dipswitch_4 (.out(dipswitch_1_out[1]));
  DipSwitch dipswitch_5 (.out(dipswitch_1_out[2]));
  DipSwitch dipswitch_6 (.out(dipswitch_2_out[0]));
  DipSwitch dipswitch_7 (.out(dipswitch_2_out[1]));
  DipSwitch dipswitch_8 (.out(dipswitch_2_out[2]));
  // Probe B on {dipswitch_12_out, dipswitch_16_out}
  Seven_Seg_Hex seven_seg_hex_3 (.d(dipswitch_12_out), .dp(1'b0));
  DipSwitch dipswitch_9 (.out(dipswitch_12_out[0]));
  DipSwitch dipswitch_10 (.out(dipswitch_12_out[1]));
  DipSwitch dipswitch_11 (.out(dipswitch_12_out[2]));
  DipSwitch dipswitch_12 (.out(dipswitch_12_out[3]));
  Seven_Seg_Hex seven_seg_hex_4 (.d(dipswitch_16_out), .dp(1'b0));
  DipSwitch dipswitch_13 (.out(dipswitch_16_out[0]));
  DipSwitch dipswitch_14 (.out(dipswitch_16_out[1]));
  DipSwitch dipswitch_15 (.out(dipswitch_16_out[2]));
  DipSwitch dipswitch_16 (.out(dipswitch_16_out[3]));
  Seven_Seg_Hex seven_seg_hex_5 (.d(addsub8b_1_r_2), .dp(1'b0));
  addsub8b addsub8b_1 (
    .A({dipswitch_1_out, dipswitch_2_out}), .B({dipswitch_12_out, dipswitch_16_out}), .sub(sub),
    .R({addsub8b_1_r_2, addsub8b_1_r}), .Co(addsub8b_1_co));
  Seven_Seg_Hex seven_seg_hex_6 (.d(addsub8b_1_r), .dp(1'b0));
  flags flags_1 (
    .A({dipswitch_1_out, dipswitch_2_out}), .B({dipswitch_12_out, dipswitch_16_out}),
    .R({addsub8b_1_r_2, addsub8b_1_r}), .sub(sub), .Z(flags_1_z), .N(flags_1_n), .O(flags_1_o));
  LED C (.in(addsub8b_1_co));
  LED Z (.in(flags_1_z));
  LED N (.in(flags_1_n));
  LED O (.in(flags_1_o));
  // Probe R on {addsub8b_1_r_2, addsub8b_1_r}
endmodule
