// Digital circuit aeqb.dig as structural Verilog
module aeqb (
  input  AEQBin,
  input  Ai,
  input  Bi,
  output AEQBout
);

  wire and_1_out, and_2_out, not_1_out, not_2_out;

  not not_1 (not_1_out, Ai);
  not not_2 (not_2_out, Bi);
  and and_1 (and_1_out, AEQBin, not_1_out, not_2_out);
  and and_2 (and_2_out, AEQBin, Ai, Bi);
  or or_1 (AEQBout, and_1_out, and_2_out);
endmodule
