// Digital circuit agtltb.dig as structural Verilog
module agtltb (
  input  AGTBin,
  input  ALTBin,
  input  Ai,
  input  Bi,
  output AGTBout,
  output ALTBout
);

  wire and_1_out, and_2_out, and_3_out, and_4_out, not_1_out, not_2_out, not_3_out, not_4_out;

  not not_1 (not_1_out, AGTBin);
  not not_2 (not_2_out, ALTBin);
  not not_3 (not_3_out, Ai);
  not not_4 (not_4_out, Bi);
  and and_1 (and_1_out, AGTBin, not_2_out);
  and and_2 (and_2_out, not_2_out, Ai, not_4_out);
  and and_3 (and_3_out, not_1_out, not_3_out, Bi);
  and and_4 (and_4_out, not_1_out, ALTBin);
  or or_1 (AGTBout, and_1_out, and_2_out);
  or or_2 (ALTBout, and_3_out, and_4_out);
endmodule
