// Digital circuit comp.dig as structural Verilog
module comp (
  input  [3:0] A,
  input  [3:0] B,
  output A_eq_B,
  output A_gt_B,
  output A_lt_B
);

  wire aeqb_1_aeqbout, aeqb_2_aeqbout, aeqb_3_aeqbout, agtltb_1_agtbout, agtltb_1_altbout, agtltb_2_agtbout,
       agtltb_2_altbout, agtltb_3_agtbout, agtltb_3_altbout;

  aeqb aeqb_1 (.AEQBout(aeqb_1_aeqbout), .AEQBin(1'b1), .Ai(A[3]), .Bi(B[3]));
  agtltb agtltb_1 (
    .AGTBout(agtltb_1_agtbout), .ALTBout(agtltb_1_altbout), .AGTBin(1'b0), .ALTBin(1'b0), .Ai(A[3]), .Bi(B[3]));
  aeqb aeqb_2 (.AEQBout(aeqb_2_aeqbout), .AEQBin(aeqb_1_aeqbout), .Ai(A[2]), .Bi(B[2]));
  agtltb agtltb_2 (
    .AGTBout(agtltb_2_agtbout), .ALTBout(agtltb_2_altbout), .AGTBin(agtltb_1_agtbout),
    .ALTBin(agtltb_1_altbout), .Ai(A[2]), .Bi(B[2]));
  aeqb aeqb_3 (.AEQBout(aeqb_3_aeqbout), .AEQBin(aeqb_2_aeqbout), .Ai(A[1]), .Bi(B[1]));
  agtltb agtltb_3 (
    .AGTBout(agtltb_3_agtbout), .ALTBout(agtltb_3_altbout), .AGTBin(agtltb_2_agtbout),
    .ALTBin(agtltb_2_altbout), .Ai(A[1]), .Bi(B[1]));
  aeqb aeqb_4 (.AEQBout(A_eq_B), .AEQBin(aeqb_3_aeqbout), .Ai(A[0]), .Bi(B[0]));
  agtltb agtltb_4 (
    .AGTBout(A_gt_B), .ALTBout(A_lt_B), .AGTBin(agtltb_3_agtbout), .ALTBin(agtltb_3_altbout), .Ai(A[0]),
    .Bi(B[0]));
endmodule
