// Digital circuit compeq.dig as structural Verilog
module compeq (
  input  [3:0] A,
  input  [3:0] B,
  output A_eq_B
);

  wire aeqb_1_aeqbout, aeqb_2_aeqbout, aeqb_3_aeqbout;

  aeqb aeqb_1 (.AEQBout(aeqb_1_aeqbout), .AEQBin(1'b1), .Ai(A[3]), .Bi(B[3]));
  aeqb aeqb_2 (.AEQBout(aeqb_2_aeqbout), .AEQBin(aeqb_1_aeqbout), .Ai(A[2]), .Bi(B[2]));
  aeqb aeqb_3 (.AEQBout(aeqb_3_aeqbout), .AEQBin(aeqb_2_aeqbout), .Ai(A[1]), .Bi(B[1]));
  aeqb aeqb_4 (.AEQBout(A_eq_B), .AEQBin(aeqb_3_aeqbout), .Ai(A[0]), .Bi(B[0]));
endmodule
