// Digital circuit compgtlt.dig as structural Verilog
module compgtlt (
  input  [3:0] A,
  input  [3:0] B,
  output A_gt_B,
  output A_lt_B
);

  wire agtltb_1_agtbout, agtltb_1_altbout, agtltb_2_agtbout, agtltb_2_altbout, agtltb_3_agtbout,
       agtltb_3_altbout;

  agtltb agtltb_1 (
    .AGTBout(agtltb_1_agtbout), .ALTBout(agtltb_1_altbout), .AGTBin(1'b0), .ALTBin(1'b0), .Ai(A[3]), .Bi(B[3]));
  agtltb agtltb_2 (
    .AGTBout(agtltb_2_agtbout), .ALTBout(agtltb_2_altbout), .AGTBin(agtltb_1_agtbout),
    .ALTBin(agtltb_1_altbout), .Ai(A[2]), .Bi(B[2]));
  agtltb agtltb_3 (
    .AGTBout(agtltb_3_agtbout), .ALTBout(agtltb_3_altbout), .AGTBin(agtltb_2_agtbout),
    .ALTBin(agtltb_2_altbout), .Ai(A[1]), .Bi(B[1]));
  agtltb agtltb_4 (
    .AGTBout(A_gt_B), .ALTBout(A_lt_B), .AGTBin(agtltb_3_agtbout), .ALTBin(agtltb_3_altbout), .Ai(A[0]),
    .Bi(B[0]));
endmodule
