// Digital circuit dec.dig as structural Verilog
module dec (
  input  N_2,
  input  N_1,
  input  N_0,
  output F
);

  wire dec2_4en_1_y1, dec2_4en_1_y2, dec2_4en_1_y3, not_1_out;

  not not_1 (not_1_out, N_0);
  dec2_4en dec2_4en_1 (
    .EN(not_1_out), .I1(N_2), .I0(N_1), .Y3(dec2_4en_1_y3), .Y2(dec2_4en_1_y2), .Y1(dec2_4en_1_y1));  // open: Y0
  or or_1 (F, dec2_4en_1_y3, dec2_4en_1_y2, dec2_4en_1_y1);
endmodule
