// Digital circuit dec2_4en.dig as structural Verilog
module dec2_4en (
  input  EN,
  input  I1,
  input  I0,
  output Y3,
  output Y2,
  output Y1,
  output Y0
);

  wire not_1_out, not_2_out;

  not not_1 (not_1_out, I1);
  not not_2 (not_2_out, I0);
  and and_1 (Y3, EN, I0, I1);
  and and_2 (Y2, EN, not_2_out, I1);
  and and_3 (Y1, EN, I0, not_1_out);
  and and_4 (Y0, EN, not_2_out, not_1_out);
endmodule
