// Digital circuit dec3_8.dig as structural Verilog
module dec3_8 (
  input  N_2,
  input  N_1,
  input  N_0,
  output F
);

  wire decoder_1_out_2, decoder_1_out_4, decoder_1_out_6;

  Decoder #(.Selector_Bits(3)) decoder_1 (
    .sel({N_2, N_1, N_0}), .out_2(decoder_1_out_2), .out_4(decoder_1_out_4), .out_6(decoder_1_out_6));  // open: out_0, out_1, out_3, out_5, out_7
  or or_1 (F, decoder_1_out_2, decoder_1_out_4, decoder_1_out_6);
endmodule
