// Digital circuit mux2_1.dig as structural Verilog
module mux2_1 (
  input  [2:0] N,
  output [5:0] N_2
);

  wire [5:0] multiplexer_1_out, multiplexer_2_out, multiplexer_3_out, multiplexer_4_out, multiplexer_5_out,
       multiplexer_6_out;

  Multiplexer #(.Bits(6)) multiplexer_1 (.sel(N[0]), .in_0({6{1'b0}}), .in_1(6'b000001), .out(multiplexer_1_out));
  Multiplexer #(.Bits(6)) multiplexer_2 (.sel(N[0]), .in_0(6'b000100), .in_1(6'b001001), .out(multiplexer_2_out));
  Multiplexer #(.Bits(6)) multiplexer_3 (.sel(N[0]), .in_0(6'b010000), .in_1(6'b011001), .out(multiplexer_3_out));
  Multiplexer #(.Bits(6)) multiplexer_4 (.sel(N[0]), .in_0(6'b100100), .in_1(6'b110001), .out(multiplexer_4_out));
  // Probe on N[0]
  Multiplexer #(.Bits(6)) multiplexer_5 (
    .sel(N[1]), .in_0(multiplexer_1_out), .in_1(multiplexer_2_out), .out(multiplexer_5_out));
  Multiplexer #(.Bits(6)) multiplexer_6 (
    .sel(N[1]), .in_0(multiplexer_3_out), .in_1(multiplexer_4_out), .out(multiplexer_6_out));
  // Probe on N[1]
  Multiplexer #(.Bits(6)) multiplexer_7 (.sel(N[2]), .in_0(multiplexer_5_out), .in_1(multiplexer_6_out), .out(N_2));
  // Probe on N[2]
endmodule
