// Digital circuit mux4_1.dig as structural Verilog
module mux4_1 (
  input  [2:0] N,
  output [5:0] N_2
);

  wire [5:0] multiplexer_1_out, multiplexer_2_out;

  Multiplexer #(.Bits(6), .Selector_Bits(2)) multiplexer_1 (
    .sel(N[1:0]), .in_0({6{1'b0}}), .in_1(6'b000001), .in_2(6'b000100), .in_3(6'b001001),
    .out(multiplexer_1_out));
  Multiplexer #(.Selector_Bits(2), .Bits(6)) multiplexer_2 (
    .sel(N[1:0]), .in_0(6'b010000), .in_1(6'b011001), .in_2(6'b100100), .in_3(6'b110001),
    .out(multiplexer_2_out));
  Multiplexer #(.Selector_Bits(2), .Bits(6)) multiplexer_3 (
    .sel(N[2:1]), .in_0(multiplexer_1_out), .in_1(multiplexer_1_out), .in_2(multiplexer_2_out),
    .in_3(multiplexer_2_out), .out(N_2));
  // Probe on N[1:0]
  // Probe on N[2:1]
endmodule
