// Digital circuit mux8_1.dig as structural Verilog
module mux8_1 (
  input  [2:0] N,
  output [5:0] N_2
);

  Multiplexer #(.Bits(6), .Selector_Bits(3)) multiplexer_1 (
    .sel(N), .in_0({6{1'b0}}), .in_1(6'b000001), .in_2(6'b000100), .in_3(6'b001001), .in_4(6'b010000),
    .in_5(6'b011001), .in_6(6'b100100), .in_7(6'b110001), .out(N_2));
endmodule
