// Digital circuit ALU.dig as structural Verilog
module ALU (
  input  [7:0] A,
  input  [7:0] B,
  input  [2:0] OPR,
  output [7:0] R,
  output [3:0] FLAGS
);

  wire addsub8b_1_co, addsub8b_2_co;
  wire [7:0] addsub8b_1_r, addsub8b_2_r, and_1_out, or_1_out, xor_1_out;

  addsub8b addsub8b_1 (.A(A), .B(B), .sub(1'b1), .R(addsub8b_1_r), .Co(addsub8b_1_co));
  addsub8b addsub8b_2 (.A(A), .B(B), .sub(1'b0), .R(addsub8b_2_r), .Co(addsub8b_2_co));
  assign xor_1_out = A ^ B;  // XOr xor_1, 8 bits wide
  assign and_1_out = A & B;  // And and_1, 8 bits wide
  assign or_1_out = A | B;  // Or or_1, 8 bits wide
  Multiplexer #(.Selector_Bits(3), .Bits(8)) multiplexer_1 (
    .sel(OPR), .in_0(B), .in_1(addsub8b_1_r), .in_2(addsub8b_2_r), .in_3(xor_1_out),
    .in_4({{2{A[7]}}, A[6:1]}), .in_5({A[6:0], 1'b0}), .in_6(and_1_out), .in_7(or_1_out), .out(R));
  // newFlags newflags_1: pin names not known; wires that end beside it: OPR, A, B, addsub8b_1_co, addsub8b_2_co, R, FLAGS

  // Notes on the sheet:
  //   OPR
  //   000
  //   001
  //   010
  //   011
  //   100
  //   101
  //   110
  //   111
  //   FLAGS
  //   [0] Z
  //   [1] N
  //   [2] C
  //   [3] O
  //   Descrição
  //   R = B
  //   R = A - B
  //   R = A + B
  //   R  =  A ^ B
  //   R = A >> 1
  //   R = A << 1
  //   R = A & B
  //   R = A | B
  //   Descrição
  //   R = 0
  //   R < 0
  //   Carry
  //   Overflow
endmodule
