// Digital circuit add8b.dig as structural Verilog
module add8b (
  input  [7:0] A,
  input  [7:0] B,
  input  Ci,
  output [7:0] S,
  output Co
);

  wire add4b_2_co;

  add4b add4b_1 (
    .A3(A[7]), .A2(A[6]), .A1(A[5]), .A0(A[4]), .B3(B[7]), .B2(B[6]), .B1(B[5]), .B0(B[4]), .Ci(add4b_2_co),
    .Co(Co), .S3(S[7]), .S2(S[6]), .S1(S[5]), .S0(S[4]));
  add4b add4b_2 (
    .A3(A[3]), .A2(A[2]), .A1(A[1]), .A0(A[0]), .B3(B[3]), .B2(B[2]), .B1(B[1]), .B0(B[0]), .Ci(Ci),
    .Co(add4b_2_co), .S3(S[3]), .S2(S[2]), .S1(S[1]), .S0(S[0]));
endmodule
