// Digital circuit flags.dig as structural Verilog
module flags (
  input  [7:0] A,
  input  [7:0] B,
  input  [7:0] R,
  input  sub,
  output Z,
  output N,
  output O
);

  wire or_1_out, or_2_out;

  or or_1 (or_1_out, R[0], R[1], R[2], R[3]);
  or or_2 (or_2_out, R[4], R[5], R[6], R[7]);
  nor nor_1 (Z, or_1_out, or_2_out);
  ovf ovf_1 (.sub(sub), .A7(A[7]), .B7(B[7]), .R7(R[7]), .ovf(O));

  assign N = R[7];
endmodule
