// Digital circuit Lab4.dig as structural Verilog
module Lab4 (
);

  wire alu_1_p5, clock_out, or_1_out, reset_2_out, reset_out;
  wire [2:0] dipswitch_11_out;
  wire [3:0] reg4_1_p5;
  wire [7:0] A, B, R;

  Button reset (.out(reset_out));
  Button clock (.out(clock_out));
  DipSwitch dipswitch_1 (.out(B[7]));
  DipSwitch dipswitch_2 (.out(B[6]));
  DipSwitch dipswitch_3 (.out(B[5]));
  DipSwitch dipswitch_4 (.out(B[4]));
  DipSwitch dipswitch_5 (.out(B[3]));
  // Probe on B
  DipSwitch dipswitch_6 (.out(B[2]));
  DipSwitch dipswitch_7 (.out(B[1]));
  DipSwitch dipswitch_8 (.out(B[0]));
  Reset #(.invertOutput("false")) reset_2 (.out(reset_2_out));
  or or_1 (or_1_out, reset_2_out, reset_out);
  // Probe on dipswitch_11_out
  DipSwitch dipswitch_9 (.out(dipswitch_11_out[2]));
  DipSwitch dipswitch_10 (.out(dipswitch_11_out[1]));
  DipSwitch dipswitch_11 (.out(dipswitch_11_out[0]));
  reg8 reg8_1 (.D(R), .en(1'b1), .rst(or_1_out), .ck(clock_out), .Q(A));
  // ALU alu_1: pin names not known; wires that end beside it: A, B, dipswitch_11_out, R, alu_1_p5
  // reg4 reg4_1: pin names not known; wires that end beside it: alu_1_p5, 1'b1, or_1_out, clock_out, reg4_1_p5
  LED led_1 (.in(reg4_1_p5[3]));
  LED led_2 (.in(reg4_1_p5[2]));
  LED led_3 (.in(reg4_1_p5[1]));
  LED led_4 (.in(reg4_1_p5[0]));
  Seven_Seg_Hex seven_seg_hex_1 (.d(R[7:4]), .dp(1'b0));
  Seven_Seg_Hex seven_seg_hex_2 (.d(R[3:0]), .dp(1'b0));
  // Probe on R
  Seven_Seg_Hex seven_seg_hex_3 (.d(A[7:4]), .dp(1'b0));
  Seven_Seg_Hex seven_seg_hex_4 (.d(A[3:0]), .dp(1'b0));
  // Probe on A
  Seven_Seg_Hex seven_seg_hex_5 (.d(B[7:4]), .dp(1'b0));
  Seven_Seg_Hex seven_seg_hex_6 (.d(B[3:0]), .dp(1'b0));
  // Probe on B

  // Notes on the sheet:
  //   LAB 4
  //   SD
  //   2023/24
  //   OPR
  //   000
  //   001
  //   010
  //   011
  //   100
  //   101
  //   110
  //   111
  //   X
  //   Descrição
  //   R = B
  //   R = A - B
  //   R = A + B
  //   R  =  A ^ B
  //   R = A >> 1
  //   R = A << 1
  //   R = A & B
  //   R = A | B
  //   OPR
  //   FLAGS
  //   [0] Z
  //   [1] N
  //   [2] C
  //   [3] O
  //   Descrição
  //   R = 0
  //   R < 0
  //   Carry
  //   Overflow
  //   O
  //   C
  //   N
  //   Z
  //   R
  //   A
  //   B
endmodule
