// Digital circuit dec24e.dig as structural Verilog
module dec24e (
  input  [1:0] in,
  input  en,
  output o0,
  output o1,
  output o2,
  output o3
);

  Decoder #(.Selector_Bits(3)) decoder_1 (
    .sel({en, in}), .out_4(o0), .out_5(o1), .out_6(o2), .out_7(o3));  // open: out_0, out_1, out_2, out_3
endmodule
