// Digital circuit lab5.dig as structural Verilog
module lab5 (
);

  wire alu_1_p5, clock_out, dec24e_1_o0, dec24e_1_o1, dec24e_1_o2, dec24e_1_o3, not_1_out, regs_out,
       reset_2_out, reset_out, rst;
  wire [1:0] dipswitch_16_out;
  wire [2:0] dipswitch_7_out, dipswitch_14_out;
  wire [3:0] multiplexer_2_out, multiplexer_4_out, multiplexer_4_out_2, multiplexer_5_out,
       multiplexer_5_out_2, reg4_1_p5;
  wire [7:0] A, B, dipswitch_12_out, multiplexer_3_out, R, R1, R2, R3;
  wire [7:4] multiplexer_2_out_2;

  // Probe on dipswitch_7_out
  DipSwitch dipswitch_1 (.out(dipswitch_7_out[2]));
  DipSwitch dipswitch_2 (.out(dipswitch_7_out[1]));
  DipSwitch dipswitch_3 (.out(dipswitch_12_out[7]));
  DipSwitch dipswitch_4 (.out(dipswitch_12_out[6]));
  DipSwitch dipswitch_5 (.out(dipswitch_12_out[5]));
  DipSwitch dipswitch_6 (.out(dipswitch_12_out[4]));
  DipSwitch dipswitch_7 (.out(dipswitch_7_out[0]));
  DipSwitch dipswitch_8 (.out(dipswitch_14_out[2]));
  Button clock (.out(clock_out));
  // Probe on dipswitch_12_out
  DipSwitch dipswitch_9 (.out(dipswitch_12_out[3]));
  DipSwitch dipswitch_10 (.out(dipswitch_12_out[2]));
  DipSwitch dipswitch_11 (.out(dipswitch_12_out[1]));
  DipSwitch dipswitch_12 (.out(dipswitch_12_out[0]));
  // Probe on dipswitch_14_out
  DipSwitch dipswitch_13 (.out(dipswitch_14_out[1]));
  DipSwitch dipswitch_14 (.out(dipswitch_14_out[0]));
  dec24e dec24e_1 (
    .in(dipswitch_16_out), .en(1'b1), .o0(dec24e_1_o0), .o1(dec24e_1_o1), .o2(dec24e_1_o2), .o3(dec24e_1_o3));
  // Probe on dipswitch_16_out
  // Probe on dipswitch_16_out
  DipSwitch dipswitch_15 (.out(dipswitch_16_out[1]));
  DipSwitch dipswitch_16 (.out(dipswitch_16_out[0]));
  reg8 reg8_1 (.D(R), .en(dec24e_1_o0), .rst(rst), .ck(clock_out), .Q(A));
  reg8 reg8_2 (.D(R), .en(dec24e_1_o1), .rst(rst), .ck(clock_out), .Q(R1));
  reg8 reg8_3 (.D(R), .en(dec24e_1_o2), .rst(rst), .ck(clock_out), .Q(R2));
  reg8 reg8_4 (.D(R), .en(dec24e_1_o3), .rst(rst), .ck(clock_out), .Q(R3));
  Multiplexer #(.Selector_Bits(3), .Bits(8)) multiplexer_1 (
    .sel(dipswitch_14_out), .in_0(A), .in_1(R1), .in_2(R2), .in_3(R3), .in_4(dipswitch_12_out), .in_5(8'h1),
    .in_6(8'hf), .in_7({{7{1'b0}}, reg4_1_p5[2]}), .out(B));
  // Probe on dipswitch_14_out
  // ALU alu_1: pin names not known; wires that end beside it: A, B, dipswitch_7_out, R, alu_1_p5
  // Probe on dipswitch_7_out
  // reg4 reg4_1: pin names not known; wires that end beside it: alu_1_p5, 1'b1, rst, clock_out, reg4_1_p5
  LED led_1 (.in(reg4_1_p5[3]));
  LED led_2 (.in(reg4_1_p5[2]));
  LED led_3 (.in(not_1_out));
  not not_1 (not_1_out, regs_out);
  LED led_4 (.in(regs_out));
  Seven_Seg_Hex seven_seg_hex_1 (.d(multiplexer_2_out_2), .dp(1'b0));
  Multiplexer #(.Bits(8)) multiplexer_2 (
    .sel(regs_out), .in_0({8{1'b0}}), .in_1(A), .out({multiplexer_2_out_2, multiplexer_2_out}));
  LED led_5 (.in(reg4_1_p5[1]));
  LED led_6 (.in(reg4_1_p5[0]));
  Seven_Seg_Hex seven_seg_hex_2 (.d(multiplexer_2_out), .dp(1'b0));
  // Probe on {multiplexer_2_out_2, multiplexer_2_out}
  // Probe on {multiplexer_2_out_2, multiplexer_2_out}
  Button reset (.out(reset_out));
  Seven_Seg_Hex seven_seg_hex_3 (.d(multiplexer_3_out[7:4]), .dp(1'b0));
  Multiplexer #(.Bits(8)) multiplexer_3 (.sel(regs_out), .in_0(R), .in_1(R1), .out(multiplexer_3_out));
  Reset #(.invertOutput("false")) reset_2 (.out(reset_2_out));
  or or_1 (rst, reset_2_out, reset_out);
  Seven_Seg_Hex seven_seg_hex_4 (.d(multiplexer_3_out[3:0]), .dp(1'b0));
  // Probe on multiplexer_3_out
  // Probe on multiplexer_3_out
  Seven_Seg_Hex seven_seg_hex_5 (.d(multiplexer_4_out_2), .dp(1'b0));
  Multiplexer #(.Bits(8)) multiplexer_4 (
    .sel(regs_out), .in_0(A), .in_1(R2), .out({multiplexer_4_out_2, multiplexer_4_out}));
  Seven_Seg_Hex seven_seg_hex_6 (.d(multiplexer_4_out), .dp(1'b0));
  // Probe on {multiplexer_4_out_2, multiplexer_4_out}
  // Probe on {multiplexer_4_out_2, multiplexer_4_out}
  Seven_Seg_Hex seven_seg_hex_7 (.d(multiplexer_5_out_2), .dp(1'b0));
  Multiplexer #(.Bits(8)) multiplexer_5 (
    .sel(regs_out), .in_0(B), .in_1(R3), .out({multiplexer_5_out_2, multiplexer_5_out}));
  Button regs (.out(regs_out));
  Seven_Seg_Hex seven_seg_hex_8 (.d(multiplexer_5_out), .dp(1'b0));
  // Probe on {multiplexer_5_out_2, multiplexer_5_out}
  // Probe on {multiplexer_5_out_2, multiplexer_5_out}

  // Notes on the sheet:
  //   LAB 5
  //   SD
  //   2023/24
  //   X
  //   OPR
  //   SEL
  //   CE
  //   C
  //   O
  //   N
  //   Z
  //   A
  //   000
  //   001
  //   010
  //   011
  //   100
  //   101
  //   110
  //   111
  //   R = B
  //   R = A - B
  //   R = A + B
  //   R  =  A ^ B
  //   R = A >> 1
  //   R = A << 1
  //   R = A & B
  //   R = A | B
  //   R
  //   R1
  //   R2
  //   A
  //   R1
  //   R2
  //   R3
  //   X
  //   1
  //   15
  //   C
  //   B
  //   R3
  //   00
  //   01
  //   10
  //   11
  //   A
  //   R1
  //   R2
  //   R3
endmodule
