// Digital circuit Circuito FSM UABOS v1.00.dig as structural Verilog
module Circuito_FSM_UABOS_v1_00 (
  input  CX,
  input  FIM,
  input  UABO,
  input  C,
  output M1,
  output M2
);

  wire and_1_out, and_2_out, and_3_out, and_4_out, and_5_out, and_6_out, and_7_out, and_8_out, not_1_out,
       not_2_out, or_1_out, or_2_out, Z_0_n, Z_1_n;

  not not_1 (not_1_out, UABO);
  not not_2 (not_2_out, Z_1_n);
  not not_3 (M2, Z_0_n);
  and and_1 (and_1_out, CX, UABO, M2);
  and and_2 (and_2_out, FIM, M2, not_2_out);
  and and_3 (and_3_out, FIM, Z_0_n, Z_1_n);
  and and_4 (and_4_out, UABO, Z_0_n, not_2_out);
  and and_5 (and_5_out, CX, not_1_out, M2);
  and and_6 (and_6_out, CX, not_1_out, not_2_out);
  and and_7 (and_7_out, FIM, M2, not_2_out);
  and and_8 (and_8_out, FIM, Z_0_n, Z_1_n);
  and and_9 (M1, Z_0_n, not_2_out);
  or or_1 (or_1_out, and_1_out, and_2_out, and_3_out, and_4_out);
  or or_2 (or_2_out, and_5_out, and_6_out, and_7_out, and_8_out);
  D_FF u_Z_1_n (.D(or_1_out), .C(C), .Q(Z_1_n));  // open: nQ
  D_FF u_Z_0_n (.D(or_2_out), .C(C), .Q(Z_0_n));  // open: nQ
  // Probe Diagrama FSM UABOS v1.00.fsm on {Z_1_n, Z_0_n}

  // Notes on the sheet:
  //   C: Hz: 2
endmodule
