// Digital circuit Circuito FSM UABOS v1.10.dig as structural Verilog
module Circuito_FSM_UABOS_v1_10 (
  input  CX,
  input  FIM,
  input  UABO,
  input  C,
  output M1,
  output M2
);

  wire and_1_out, and_2_out, and_3_out, and_4_out, and_5_out, and_6_out, not_1_out, not_2_out, not_3_out,
       or_1_out, or_2_out, Z_0_n, Z_1_n;

  not not_1 (not_1_out, CX);
  not not_2 (not_2_out, UABO);
  not not_3 (not_3_out, Z_1_n);
  not not_4 (M2, Z_0_n);
  and and_1 (and_1_out, CX, UABO);
  and and_2 (and_2_out, UABO, Z_0_n);
  and and_3 (and_3_out, UABO, not_3_out);
  and and_4 (and_4_out, not_1_out, UABO, M2, not_3_out);
  and and_5 (and_5_out, not_1_out, UABO, Z_0_n, Z_1_n);
  and and_6 (and_6_out, CX, not_2_out);
  and and_7 (M1, Z_0_n, not_3_out);
  or or_1 (or_1_out, and_1_out, FIM, and_2_out, and_3_out);
  or or_2 (or_2_out, and_4_out, and_5_out, and_6_out, FIM);
  D_FF u_Z_1_n (.D(or_1_out), .C(C), .Q(Z_1_n));  // open: nQ
  D_FF u_Z_0_n (.D(or_2_out), .C(C), .Q(Z_0_n));  // open: nQ
  // Probe Diagrama FSM UABOS v1.10.fsm on {Z_1_n, Z_0_n}

  // Notes on the sheet:
  //   C: Hz: 2
endmodule
