// Digital circuit Circuito UABOS v1.00.dig as structural Verilog
module Circuito_UABOS_v1_00 (
  input  CX,
  input  UABO,
  input  FIM,
  output M1,
  output M2
);

  wire and_2_out, and_3_out;

  and and_1 (M1, CX, ~UABO, ~FIM);  // And
  and and_2 (and_2_out, CX, UABO, ~FIM);  // And
  and and_3 (and_3_out, ~CX, ~UABO, ~FIM);  // And
  or or_1 (M2, and_2_out, and_3_out);
endmodule
