// Digital circuit Circuito UABOS v1.01.dig as structural Verilog
module Circuito_UABOS_v1_01 (
  input  CX,
  input  UABO,
  input  FIM,
  output M1,
  output M2
);

  wire and_1_out, and_3_out, and_4_out;

  and and_1 (and_1_out, CX, UABO);
  and and_2 (M1, CX, ~and_1_out, ~FIM);  // And
  and and_3 (and_3_out, CX, and_1_out, ~FIM);  // And
  and and_4 (and_4_out, ~CX, ~and_1_out, ~FIM);  // And
  or or_1 (M2, and_3_out, and_4_out);
endmodule
