// Digital circuit ovf.dig as structural Verilog
module ovf (
  input  sub,
  input  A7,
  input  B7,
  input  R7,
  output ovf
);

  wire and_1_out, and_2_out, and_3_out, and_4_out, not_1_out, not_2_out, not_3_out, not_4_out;

  not not_1 (not_1_out, sub);
  not not_2 (not_2_out, A7);
  not not_3 (not_3_out, B7);
  not not_4 (not_4_out, R7);
  and and_1 (and_1_out, not_2_out, not_3_out, R7, not_1_out);
  and and_2 (and_2_out, A7, B7, not_4_out, not_1_out);
  and and_3 (and_3_out, not_2_out, B7, R7, sub);
  and and_4 (and_4_out, A7, not_3_out, not_4_out, sub);
  or or_1 (ovf, and_1_out, and_2_out, and_3_out, and_4_out);
endmodule
