// Digital circuit newFlags.dig as structural Verilog
module newFlags (
  input  [2:0] OPR,
  input  [7:0] A,
  input  [7:0] B,
  input  Csub,
  input  Cadd,
  input  [7:0] R,
  output [3:0] FLAGS
);

  wire decoder_1_out_1, decoder_1_out_2, flags_1_o, or_1_out;

  Multiplexer #(.Selector_Bits(3)) multiplexer_1 (
    .sel(OPR), .in_0(1'b0), .in_1(Csub), .in_2(Cadd), .in_3(1'b0), .in_4(1'b0), .in_5(1'b0), .in_6(1'b0),
    .in_7(1'b0), .out(FLAGS[2]));
  Decoder #(.Selector_Bits(3)) decoder_1 (
    .sel(OPR), .out_1(decoder_1_out_1), .out_2(decoder_1_out_2));  // open: out_0, out_3, out_4, out_5, out_6, out_7
  flags flags_1 (.A(A), .B(B), .R(R), .sub(decoder_1_out_1), .Z(FLAGS[0]), .N(FLAGS[1]), .O(flags_1_o));
  or or_1 (or_1_out, decoder_1_out_1, decoder_1_out_2);
  Multiplexer multiplexer_2 (.sel(or_1_out), .in_0(1'b0), .in_1(flags_1_o), .out(FLAGS[3]));
  // Pins of 1 and 4 bits meet at FLAGS
endmodule
