// Digital circuit reg4.dig as structural Verilog
module reg4 (
  input  [7:0] D,
  input  en,
  input  rst,
  input  ck,
  output [3:0] Q
);

  wire [3:0] multiplexer_1_out;

  Multiplexer #(.Bits(4)) multiplexer_1 (.sel(en), .in_0(Q), .in_1(D[3:0]), .out(multiplexer_1_out));
  D_FF_AS #(.Bits(4)) d_ff_as_1 (.Set(1'b0), .D(multiplexer_1_out), .C(ck), .Clr(rst), .Q(Q));  // open: nQ
  // Pins of 4 and 8 bits meet at D
endmodule
