// Digital circuit cnt5.dig as structural Verilog
module cnt5 (
  input  Ck,
  input  Rst,
  input  Ld,
  input  [4:0] D,
  output [4:0] Q
);

  wire [4:0] add_1_s, multiplexer_1_out;

  Add #(.Bits(5)) add_1 (.a(Q), .b(5'b00001), .c_i(1'b0), .s(add_1_s));  // open: c_o
  Multiplexer #(.Bits(5)) multiplexer_1 (.sel(Ld), .in_0(add_1_s), .in_1(D), .out(multiplexer_1_out));
  D_FF_AS #(.Bits(5)) d_ff_as_1 (.Set(1'b0), .D(multiplexer_1_out), .C(Ck), .Clr(Rst), .Q(Q));  // open: nQ
endmodule
