// Digital circuit lab7b.dig as structural Verilog
module lab7b (
  input  regs
);

  wire alu_1_p5, and_1_out, clk, comparator_1_eq, dec24e_1_o0, dec24e_1_o1, dec24e_1_o2, dec24e_1_o3,
       not_1_out, not_2_out, not_3_out, reset_2_out, reset_out, rst;
  wire [1:0] mem_1_d;
  wire [3:0] reg4_1_p5;
  wire [4:0] addr;
  wire [7:0] A, B, d0, d1, d2, d3, R, R1, R2, R3, X;
  wire [7:2] mem_1_d_2;

  and and_1 (and_1_out, ~reg4_1_p5[0], comparator_1_eq);  // And
  cnt5 cnt5_1 (.Ck(clk), .Rst(rst), .Ld(and_1_out), .D({mem_1_d_2[4:2], mem_1_d}), .Q(addr));
  LED led_1 (.in(mem_1_d_2[7]));
  mem mem_1 (.A(addr), .D({mem_1_d_2, mem_1_d}));
  LED led_2 (.in(mem_1_d_2[6]));
  LED led_3 (.in(mem_1_d_2[5]));
  // Probe on {mem_1_d_2, mem_1_d}
  LED led_4 (.in(mem_1_d_2[4]));
  LED led_5 (.in(mem_1_d_2[3]));
  dec24e dec24e_1 (
    .in(mem_1_d), .en(not_1_out), .o0(dec24e_1_o0), .o1(dec24e_1_o1), .o2(dec24e_1_o2), .o3(dec24e_1_o3));
  not not_1 (not_1_out, comparator_1_eq);
  LED led_6 (.in(mem_1_d_2[2]));
  LED led_7 (.in(mem_1_d[1]));
  LED led_8 (.in(mem_1_d[0]));
  Comparator #(.Bits(3)) comparator_1 (.a(mem_1_d_2[7:5]), .b(3'b101), .eq(comparator_1_eq));  // open: gt, lt
  reg8 reg8_1 (.D(R), .en(dec24e_1_o0), .rst(rst), .ck(clk), .Q(A));
  reg8 reg8_2 (.D(R), .en(dec24e_1_o1), .rst(rst), .ck(clk), .Q(R1));
  reg8 reg8_3 (.D(R), .en(dec24e_1_o2), .rst(rst), .ck(clk), .Q(R2));
  reg8 reg8_4 (.D(R), .en(dec24e_1_o3), .rst(rst), .ck(clk), .Q(R3));
  Multiplexer #(.Selector_Bits(3), .Bits(8)) multiplexer_1 (
    .sel(mem_1_d_2[4:2]), .in_0(A), .in_1(R1), .in_2(R2), .in_3(R3), .in_4(X), .in_5(8'h1), .in_6(8'hf),
    .in_7({{7{1'b0}}, reg4_1_p5[2]}), .out(B));
  // ALU alu_1: pin names not known; wires that end beside it: A, B, mem_1_d_2[7:5], R, alu_1_p5
  not not_2 (not_2_out, comparator_1_eq);
  // reg4 reg4_1: pin names not known; wires that end beside it: alu_1_p5, not_2_out, rst, clk, reg4_1_p5
  LED led_9 (.in(reg4_1_p5[3]));
  LED led_10 (.in(reg4_1_p5[2]));
  LED led_11 (.in(not_3_out));
  not not_3 (not_3_out, regs);
  LED led_12 (.in(regs));
  Seven_Seg_Hex seven_seg_hex_1 (.d(d0[7:4]), .dp(1'b0));
  Multiplexer #(.Bits(8)) multiplexer_2 (.sel(regs), .in_0({3'b000, addr}), .in_1(A), .out(d0));
  LED led_13 (.in(reg4_1_p5[1]));
  LED led_14 (.in(reg4_1_p5[0]));
  Seven_Seg_Hex seven_seg_hex_2 (.d(d0[3:0]), .dp(1'b0));
  Button reset (.out(reset_out));
  Button clock (.out(clk));
  Seven_Seg_Hex seven_seg_hex_3 (.d(d1[7:4]), .dp(1'b0));
  Multiplexer #(.Bits(8)) multiplexer_3 (.sel(regs), .in_0(R), .in_1(R1), .out(d1));
  Reset #(.invertOutput("false")) reset_2 (.out(reset_2_out));
  DipSwitch dipswitch_1 (.out(X[7]));
  Seven_Seg_Hex seven_seg_hex_4 (.d(d1[3:0]), .dp(1'b0));
  or or_1 (rst, reset_2_out, reset_out);
  DipSwitch dipswitch_2 (.out(X[6]));
  DipSwitch dipswitch_3 (.out(X[5]));
  DipSwitch dipswitch_4 (.out(X[4]));
  DipSwitch dipswitch_5 (.out(X[3]));
  Seven_Seg_Hex seven_seg_hex_5 (.d(d2[7:4]), .dp(1'b0));
  Multiplexer #(.Bits(8)) multiplexer_4 (.sel(regs), .in_0(A), .in_1(R2), .out(d2));
  // Probe on X
  DipSwitch dipswitch_6 (.out(X[2]));
  DipSwitch dipswitch_7 (.out(X[1]));
  DipSwitch dipswitch_8 (.out(X[0]));
  Seven_Seg_Hex seven_seg_hex_6 (.d(d2[3:0]), .dp(1'b0));
  Seven_Seg_Hex seven_seg_hex_7 (.d(d3[7:4]), .dp(1'b0));
  Multiplexer #(.Bits(8)) multiplexer_5 (.sel(regs), .in_0(B), .in_1(R3), .out(d3));
  Seven_Seg_Hex seven_seg_hex_8 (.d(d3[3:0]), .dp(1'b0));

  // Notes on the sheet:
  //   LAB 7b
  //   SD
  //   2023/24
  //   OPR
  //   SEL
  //   CE
  //   JNZ?
  //   C
  //   O
  //   N
  //   Z
  //   Addr
  //   A
  //   X
  //   R
  //   R1
  //   R2
  //   B
  //   R3
endmodule
