// Digital circuit mem.dig as structural Verilog
module mem (
  input  [4:0] A,
  output [7:0] D
);

  Multiplexer #(.Selector_Bits(5), .Bits(8)) multiplexer_1 (
    .sel(A), .in_0(8'h20), .in_1(8'h2), .in_2(8'h11), .in_3(8'ha7), .in_4(8'hb), .in_5(8'h15), .in_6(8'ha6),
    .in_7(8'h44), .in_8(8'h40), .in_9(8'h40), .in_10(8'h40), .in_11(8'h40), .in_12(8'h40), .in_13(8'h40),
    .in_14(8'h40), .in_15(8'ha2), .in_16(8'h8), .in_17(8'h56), .in_18(8'h20), .in_19(8'h15), .in_20(8'ha2),
    .in_21({8{1'b0}}), .in_22({8{1'b0}}), .in_23({8{1'b0}}), .in_24({8{1'b0}}), .in_25({8{1'b0}}),
    .in_26({8{1'b0}}), .in_27({8{1'b0}}), .in_28({8{1'b0}}), .in_29({8{1'b0}}), .in_30({8{1'b0}}),
    .in_31({8{1'b0}}), .out(D));
endmodule
